# Fritzing sketch L9110 (saved by Fritzing 1.0.1rc)
breadboards: 1

parts:
  A1 = Raspberry Pi Pico H
  F1 = Small Fan, based on Fan - Ventilador [package=THT]
  U1 = L9110 H-bridge module [part_number="L9110 H-bridge"]
  J1 = 2.1mm Barrel Jack with Terminal Block

nets:
  N1: A1.GP0, U1.B-IA
  N2: A1.GP1, U1.B-IB
  GND: A1.GND, U1.GND, J1.NEG
  N3: F1.5V, U1.MOTOR_B-B
  N4: F1.GND, U1.MOTOR_B-A
  N5: U1.VCC, J1.POS

notes:
  12 V Power
  USB Power

custom parts:
  Raspberry Pi Pico H: Raspberry Pi Pico H. Based around the RP2040 microcontroller the Pico H is a low cost microcontroller device bringing Raspberry Pi quality, cost, and easy of use to the microcontroller space.
  Small Fan, based on Fan - Ventilador: Small 2-pin fan, commonly used with single-board computers, 3d-printers, etc. This work is based on a much larger fan, as commonly found in desktop computers
